# Fritzing sketch połaczenia (saved by Fritzing 0.7.0b)
breadboards: 1

parts:
  Arduino1 = Arduino
  IC1 = L293D [package=THT]
  M1 = DC Motor
  M2 = DC Motor
  VCC1 = Battery

nets:
  N1: Arduino1.D5, IC1.In_4
  N2: Arduino1.D4, IC1.In_3
  N3: Arduino1.D3, IC1.In_1
  N4: Arduino1.D2, IC1.In_2
  N5: Arduino1.+5V, IC1.+V
  N6: Arduino1.A4, IC1.Enable_1
  N7: Arduino1.A5, IC1.Enable_2
  N8: IC1.Out_1_(_Controlled_by_Enable_1_), M2.pin_2
  N9: IC1.0V, IC1.+Vmotor, VCC1.-, VCC1.+
  N10: IC1.Out_2_(_Controlled_by_Enable_1_), M2.pin_1
  N11: IC1.Out_3_(_Controlled_by_Enable_2_), M1.pin_2
  N12: IC1.Out_4_(_Controlled_by_Enable_2_), M1.pin_1
